# Fritzing sketch Sketch_AirThermometer (saved by Fritzing 0.9.3b)
breadboards: 1

parts:
  Part1 = Arduino Uno (Rev3)
  7_Segment1 = 7 Segment Display
  R1 = Resistor [tolerance=±5% resistance=220 package=THT]
  R2 = Resistor [tolerance=±5% resistance=220 package=THT]
  R3 = Resistor [tolerance=±5% resistance=220 package=THT]
  R4 = Resistor [tolerance=±5% resistance=220 package=THT]
  R5 = Resistor [tolerance=±5% resistance=220 package=THT]
  R6 = Resistor [tolerance=±5% resistance=220 package=THT]
  R7 = Resistor [tolerance=±5% resistance=220 package=THT]
  R8 = Resistor [tolerance=±5% resistance=220 package=THT]
  R9 = Resistor [tolerance=±5% resistance=220 package=THT]
  LED2 = LED - 5mm [color="Red (633nm)" package="5 mm [THT]"]
  LED3 = LED - 5mm [color="Red (633nm)" package="5 mm [THT]"]
  R10 = Resistor [tolerance=±5% resistance=220 package=THT]
  LED4 = LED - 5mm [color="Red (633nm)" package="5 mm [THT]"]
  T1 = LM35 Temperature Sensor [package="TO92 [THT]"]

nets:
  N1: Part1.A0, T1.Vout
  N2: Part1.D8, R1.Pin_0
  N3: Part1.D9_PWM, R4.Pin_0
  N4: Part1.D10_PWM/SS, R7.Pin_0
  N5: Part1.D11_PWM/MOSI, R8.Pin_0
  N6: Part1.D2, R10.Pin_1
  N7: Part1.D3_PWM, R9.Pin_1
  N8: Part1.D4, R5.Pin_1
  N9: Part1.D5_PWM, R6.Pin_1
  N10: Part1.D6_PWM, R3.Pin_1
  N11: Part1.D7, R2.Pin_1
  N12: Part1.5V, 7_Segment1.common_anode, LED3.cathode, LED4.cathode, T1.+Vs
  GND: Part1.GND, T1.GND
  N13: 7_Segment1.Segment_G, R3.Pin_0
  N14: 7_Segment1.Segment_F, R2.Pin_0
  N15: 7_Segment1.Segment_E, R1.Pin_1
  N16: 7_Segment1.Segment_D, R4.Pin_1
  N17: 7_Segment1.Segment_DP, R7.Pin_1
  N18: 7_Segment1.Segment_C, R8.Pin_1
  N19: 7_Segment1.Segment_B, R6.Pin_0
  N20: 7_Segment1.Segment_A, R5.Pin_0
  N21: R9.Pin_0, LED2.anode
  N22: LED2.cathode, LED4.anode
  N23: LED3.anode, R10.Pin_0
